# Fritzing sketch feather_huzzah_LED (saved by Fritzing 0.9.3b)
breadboards: 1

parts:
  Part1 = Adafruit Feather HUZZAH ESP8266 [part_number="Adafruit #2821"]
  LED1 = LED - 5mm [color="Red (633nm)" package="5 mm [THT]"]
  R1 = Resistor [tolerance=±5% resistance=330 package=THT]

nets:
  N1: Part1.GND, R1.Pin_1
  N2: Part1.GPIO15, LED1.anode
  N3: LED1.cathode, R1.Pin_0

custom parts:
  Adafruit Feather HUZZAH ESP8266: his is the Adafruit Feather HUZZAH ESP8266 - our take on an 'all-in-one' ESP8266 WiFi development board with built in USB and battery charging. Its an ESP8266 WiFi module with all the extras you need, ready to rock! We have other boards in the Feather family, check'em out here. At the Feather HUZZAH's heart is an ESP8266 WiFi microcontroller clocked at 80 MHz and at 3.3V logic. This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
